# Fritzing sketch leo2mdx (saved by Fritzing 0.9.2b)
breadboards: 1

parts:
  IC1 = IC, DIP package, 20 pins [chip_label=MAX233]
  Part1 = DB25M
  Part2 = Arduino Uno (Rev3)
  C1 = Electrolytic Capacitor [capacitance=0.1mF package="100 mil [THT, electrolytic]"]

nets:
  N1: IC1.pin1, Part2.D3_PWM
  N2: IC1.pin2, Part2.D1/TX
  N3: IC1.pin3, Part2.D0/RX
  N4: IC1.pin4, Part1.pin1
  N5: IC1.pin5, Part1.pin2
  N6: IC1.pin6, Part2.GND, C1.+
  N7: IC1.pin7, Part2.VIN, C1.-
  N8: IC1.pin9, Part1.pin3
  N9: IC1.pin10, IC1.pin16
  N10: IC1.pin11, IC1.pin15
  N11: IC1.pin18, Part1.pin5
  N12: IC1.pin19, Part1.pin4
  N13: IC1.pin20, Part2.D2

notes:
  these pin connections are random, need to look closer at the real hardware.
  these bottom few connections weren't clear on the photos and might be wrong.
